# Fritzing sketch drumkid breadboard (saved by Fritzing 0.9.3b)
breadboards: 1

parts:
  S1 = Pushbutton [package="[THT]"]
  S2 = Pushbutton [package="[THT]"]
  S3 = Pushbutton [package="[THT]"]
  R1 = Rotary Potentiometer (Large) [maximum_resistance=10kΩ package=THT]
  R2 = Rotary Potentiometer (Large) [maximum_resistance=10kΩ package=THT]
  R3 = Rotary Potentiometer (Large) [maximum_resistance=10kΩ package=THT]
  S4 = Pushbutton [package="[THT]"]
  S5 = Pushbutton [package="[THT]"]
  S6 = Pushbutton [package="[THT]"]
  R4 = Rotary Potentiometer (Large) [maximum_resistance=10kΩ package=THT]
  TRS1 = Audio Jack (TRS) 3.5mm [package="4Ucon 08780 [THT]"]
  C1 = Electrolytic Capacitor [capacitance=10µF package="100 mil [THT, electrolytic]"]
  C2 = Electrolytic Capacitor [capacitance=0.22mF package="200 mil [THT, electrolytic]"]
  C3 = Electrolytic Capacitor [capacitance=10µF package="100 mil [THT, electrolytic]"]
  C4 = Electrolytic Capacitor [capacitance=2.2µF package="100 mil [THT, electrolytic]"]
  C5 = Ceramic Capacitor [capacitance=220nF package="100 mil [THT, multilayer]"]
  R5 = Resistor [tolerance=±5% resistance=470 package=THT]
  R6 = Resistor [tolerance=±5% resistance=47 package=THT]
  R7 = Resistor [tolerance=±5% resistance=10k package=THT]
  C6 = Ceramic Capacitor [capacitance=100nF package="100 mil [THT, multilayer]"]
  C7 = Ceramic Capacitor [capacitance=100nF package="100 mil [THT, multilayer]"]
  R8 = Resistor [tolerance=±5% resistance=10 package=THT]
  R9 = Resistor [tolerance=±5% resistance=1k package=THT]
  Part1 = Arduino Uno (Rev3)
  LED1 = LED - 5mm [color="Green (560nm)" package="5 mm [THT]"]
  R10 = Resistor [tolerance=±5% resistance=220 package=THT]
  R11 = Resistor [tolerance=±5% resistance=220 package=THT]
  R12 = Resistor [tolerance=±5% resistance=220 package=THT]
  R13 = Resistor [tolerance=±5% resistance=220 package=THT]
  R14 = Resistor [tolerance=±5% resistance=220 package=THT]
  LED2 = LED - 5mm [color="Green (560nm)" package="5 mm [THT]"]
  LED3 = LED - 5mm [color="Green (560nm)" package="5 mm [THT]"]
  LED4 = LED - 5mm [color="Green (560nm)" package="5 mm [THT]"]
  LED5 = LED - 5mm [color="Green (560nm)" package="5 mm [THT]"]
  R15 = Rotary Potentiometer (Large) [maximum_resistance=10kΩ package=THT]
  IC1 = IC, DIP package, 8 pins [chip_label=LM386]

nets:
  N1: S1.Pin_1, S1.Pin_2, Part1.D2
  N2: S1.Pin_3, S1.Pin_4, S2.Pin_3, S2.Pin_4, S3.Pin_3, S3.Pin_4, R1.leg2, R2.leg2, R3.leg2, S4.Pin_3, S4.Pin_4, S5.Pin_3, S5.Pin_4, S6.Pin_3, S6.Pin_4, R4.leg2, TRS1.Sleeve, C1.-, C4.-, C5.0, C6.1, R8.Pin_1, R9.Pin_0, Part1.GND, LED1.cathode, LED2.cathode, LED3.cathode, LED4.cathode, LED5.cathode, R15.leg2, IC1.pin2, IC1.pin4
  N3: S2.Pin_1, S2.Pin_2, Part1.D3_PWM
  N4: S3.Pin_1, S3.Pin_2, Part1.D4
  N5: R1.leg1, R2.leg1, R3.leg1, C6.0, Part1.5V, R15.leg1, IC1.pin6
  N6: R1.wiper, Part1.A0
  N7: R2.wiper, Part1.A1
  N8: R3.wiper, Part1.A2
  N9: S4.Pin_1, S4.Pin_2, Part1.D12/MISO
  N10: S5.Pin_1, S5.Pin_2, Part1.D11_PWM/MOSI
  N11: S6.Pin_1, S6.Pin_2, Part1.D10_PWM/SS
  N12: R4.leg1, C3.-
  N13: R4.wiper, R7.Pin_0
  N14: TRS1.Ring, TRS1.Tip, C2.-
  N15: C1.+, IC1.pin7
  N16: C2.+, C7.0, IC1.pin5
  N17: C3.+, C5.1, R5.Pin_1
  N18: C4.+, R5.Pin_0, R6.Pin_1
  N19: R6.Pin_0, Part1.D9_PWM
  N20: R7.Pin_1, R9.Pin_1, IC1.pin3
  N21: C7.1, R8.Pin_0
  N22: Part1.A3, R15.wiper
  N23: Part1.D8, R10.Pin_1
  N24: Part1.D13/SCK, R11.Pin_1
  N25: Part1.D5_PWM, R12.Pin_1
  N26: Part1.D6_PWM, R14.Pin_1
  N27: Part1.D7, R13.Pin_1
  N28: LED1.anode, R13.Pin_0
  N29: R10.Pin_0, LED2.anode
  N30: R11.Pin_0, LED3.anode
  N31: R12.Pin_0, LED5.anode
  N32: R14.Pin_0, LED4.anode
