# Fritzing sketch breadboard (saved by Fritzing 0.9.3b)
breadboards: 2

parts:
  Part1 = Arduino Nano (Rev3.0)
  S1 = Tactile Switch Buttons - 12mm Square [package=tactile-pth-12mm]
  S2 = Tactile Switch Buttons - 12mm Square [package=tactile-pth-12mm]
  S3 = Tactile Switch Buttons - 12mm Square [package=tactile-pth-12mm]
  S4 = Tactile Switch Buttons - 12mm Square [package=tactile-pth-12mm]
  S5 = Tactile Switch Buttons - 12mm Square [package=tactile-pth-12mm]
  S6 = Tactile Switch Buttons - 12mm Square [package=tactile-pth-12mm]
  U1 = POT [package=pot_alpha_rv16af-20]
  U2 = POT [package=pot_alpha_rv16af-20]
  U3 = POT [package=pot_alpha_rv16af-20]
  U4 = POT [package=pot_alpha_rv16af-20]
  U5 = MIDI_CONN_FEMALE [package=din_5_female]
  U6 = MIDI_CONN_FEMALE [package=din_5_female]
  IC1 = IC, DIP package, 8 pins [chip_label=6N138]
  U7 = POT [package=pot_alpha_rv16af-20]
  Part2 = Audio Jack Breakout
  LED1 = LED - 5mm [color="Red (633nm)" package="5 mm [THT]"]
  LED2 = LED - 5mm [color="Red (633nm)" package="5 mm [THT]"]
  LED3 = LED - 5mm [color="Red (633nm)" package="5 mm [THT]"]
  LED4 = LED - 5mm [color="Red (633nm)" package="5 mm [THT]"]
  LED5 = LED - 5mm [color="Red (633nm)" package="5 mm [THT]"]
  LED6 = LED - 5mm [color="Red (633nm)" package="5 mm [THT]"]
  R1 = Resistor [tolerance=±5% resistance=470 package=THT]
  R2 = Resistor [tolerance=±5% resistance=470 package=THT]
  R3 = Resistor [tolerance=±5% resistance=470 package=THT]
  R4 = Resistor [tolerance=±5% resistance=470 package=THT]
  R5 = Resistor [tolerance=±5% resistance=470 package=THT]
  R6 = Resistor [tolerance=±5% resistance=470 package=THT]
  R7 = Resistor [tolerance=±5% resistance=220 package=THT]
  R8 = Resistor [tolerance=±5% resistance=220 package=THT]
  S7 = Toggle Switch [package=THT]
  R9 = Resistor [tolerance=±5% resistance=10k package=THT]
  R10 = Resistor [tolerance=±5% resistance=470 package=THT]
  D1 = Diode [package=diode-1n4148]
  R11 = Resistor [tolerance=±5% resistance=220 package=THT]

nets:
  N1: Part1.D1/TX, R7.Pin_0
  N2: Part1.D0/RX, S7.L1
  GND: Part1.GND, S1.2, S1.4, S2.2, S2.4, S3.2, S3.4, S4.2, S4.4, S5.2, S5.4, S6.2, S6.4, U1.E, U2.E, U3.E, U4.E, U6.NC1, IC1.pin5, U7.E, Part2.GND, LED1.cathode, LED2.cathode, LED3.cathode, LED4.cathode, LED5.cathode, LED6.cathode, S7.COM, R9.Pin_0
  N3: Part1.D2, R5.Pin_1
  N4: Part1.D3, R4.Pin_1
  N5: Part1.D4, S4.1, S4.3
  N6: Part1.D5, S5.1, S5.3
  N7: Part1.D6, S6.1, S6.3
  N8: Part1.D7, S3.1, S3.3
  N9: Part1.D8, S2.1, S2.3
  N10: Part1.D9, U7.A
  N11: Part1.D10, S1.1, S1.3
  N12: Part1.D11/MOSI, R3.Pin_1
  N13: Part1.D12/MISO, R2.Pin_1
  N14: Part1.5V, U1.A, U2.A, U3.A, U4.A, IC1.pin8, R6.Pin_1, R8.Pin_0, R10.Pin_0
  N15: Part1.A3, U4.S
  N16: Part1.A2, U3.S
  N17: Part1.A1, U2.S
  N18: Part1.A0, U1.S
  N19: Part1.D13/SCK, R1.Pin_1
  N20: U5.MIDI_IN, IC1.pin3, D1.A
  N21: U5.MIDI_OUT, R11.Pin_1
  N22: U6.MIDI_IN, R7.Pin_1
  N23: U6.MIDI_OUT, R8.Pin_1
  N24: IC1.pin2, D1.C, R11.Pin_0
  N25: IC1.pin6, R10.Pin_1
  N26: IC1.pin7, R9.Pin_1
  N27: U7.S, Part2.RING, Part2.TIP
  N28: LED1.anode, R1.Pin_0
  N29: LED2.anode, R2.Pin_0
  N30: LED3.anode, R3.Pin_0
  N31: LED4.anode, R4.Pin_0
  N32: LED5.anode, R5.Pin_0
  N33: LED6.anode, R6.Pin_0

custom parts:
  Tactile Switch Buttons - 12mm Square: Medium-sized clicky momentary switches are standard input "buttons" on electronic projects. These work best in a PCB but can be used on a solderless breadboard as shown in this tutorial. The pins are normally open (disconnected) and when the button is pressed they are momentarily closed. They come in a pack of 10, they're pretty handy so you'll want to keep them around. You can find an EAGLE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
